// Digital circuit Design2.dig as structural Verilog
module Design2 (
  input  L,
  input  R,
  input  CLK,
  output Q2,
  output Q1,
  output Q0
);

  wire and_1_out, and_2_out, and_3_out, and_4_out, and_5_out, and_6_out, and_7_out, and_8_out, and_9_out,
       and_10_out, and_11_out, and_12_out, and_13_out, and_14_out, and_15_out, or_1_out, or_2_out, or_3_out,
       or_4_out, or_5_out, Q0_t, Q1_t, Q2_t;

  and and_1 (and_1_out, L, ~R, Q1_t);  // And
  and and_2 (and_2_out, L, ~R, Q2_t, Q0_t);  // And
  and and_3 (and_3_out, R, Q1_t);
  and and_4 (and_4_out, L, ~R);  // And
  and and_5 (and_5_out, L, R, Q0_t);
  and and_6 (and_6_out, ~L, R, Q2_t, Q0);  // And
  and and_7 (and_7_out, L, ~R, Q2_t);  // And
  and and_8 (and_8_out, L, R, Q0);
  and and_9 (and_9_out, R, Q2, Q0_t);
  and and_10 (and_10_out, ~L, R);  // And
  and and_11 (and_11_out, L, Q1);
  and and_12 (and_12_out, L, ~R, Q0_t);  // And
  and and_13 (and_13_out, R, Q2);
  and and_14 (and_14_out, L, Q2_t);
  and and_15 (and_15_out, ~L, R, Q1_t);  // And
  or or_1 (or_1_out, and_1_out, and_2_out);
  or or_2 (or_2_out, and_4_out, and_5_out, and_6_out);
  or or_3 (or_3_out, and_7_out, and_8_out, and_9_out);
  or or_4 (or_4_out, and_10_out, and_11_out, and_12_out);
  or or_5 (or_5_out, and_13_out, and_14_out, and_15_out);
  JK_FF jk_ff_1 (.J(or_1_out), .C(CLK), .K(and_3_out), .Q(Q2), .nQ(Q2_t));
  JK_FF jk_ff_2 (.J(or_2_out), .C(CLK), .K(or_3_out), .Q(Q1), .nQ(Q1_t));
  JK_FF jk_ff_3 (.J(or_4_out), .C(CLK), .K(or_5_out), .Q(Q0), .nQ(Q0_t));
endmodule
